// Logisim project Project4GivenALT.circ as structural Verilog: 14 circuits, main circuit main
module main (
  input  [3:0] in_1,
  input  [3:0] in_2,
  input  [3:0] in_3,
  input  [3:0] in_4,
  input  [3:0] in_5
);

  wire CLK, keyboard_1_avail, keyboard_2_avail, keyboarddriver_1_read, keyboarddriver_2_read,
       pull_resistor_1_node, ttydriver_1_write, ttydriver_2_write, ttydriver_3_write, vpwbmonitor_1_last_fe;
  wire [3:0] vpwbmonitor_1_last_addr;
  wire [6:0] keyboard_1_data, keyboard_2_data, ttydriver_1_data, ttydriver_2_data, ttydriver_3_data;
  wire [7:0] vpwbmonitor_1_last_data;
  wire [24:0] vpwbmonitor_1_out_4;
  wire [31:0] vpwbmonitor_1_out_3;

  Clock clock_1 (.out(CLK));
  Keyboard keyboard_1 (
    .clk(CLK), .re(keyboarddriver_1_read), .avail(keyboard_1_avail), .data(keyboard_1_data));  // open: clr
  Keyboard keyboard_2 (
    .clk(CLK), .re(keyboarddriver_2_read), .avail(keyboard_2_avail), .data(keyboard_2_data));  // open: clr
  Pull_Resistor #(.pull(1)) pull_resistor_1 (.node(pull_resistor_1_node));
  KeyboardDriver keyboarddriver_1 (
    .DATA(keyboard_1_data), .DEST(in_1), .DR(keyboard_1_avail), .CLK(CLK), .RXIN(pull_resistor_1_node),
    .READ(keyboarddriver_1_read), .TXOUT(pull_resistor_1_node));
  KeyboardDriver keyboarddriver_2 (
    .DATA(keyboard_2_data), .DEST(in_3), .DR(keyboard_2_avail), .CLK(CLK), .RXIN(pull_resistor_1_node),
    .READ(keyboarddriver_2_read), .TXOUT(pull_resistor_1_node));
  // Probe on vpwbmonitor_1_out_3
  VPWBMonitor vpwbmonitor_1 (
    .RXIN(pull_resistor_1_node), .CLK(CLK), .LAST_FE(vpwbmonitor_1_last_fe),
    .LAST_ADDR(vpwbmonitor_1_last_addr), .LAST_DATA(vpwbmonitor_1_last_data), .out_3(vpwbmonitor_1_out_3),
    .out_4(vpwbmonitor_1_out_4));
  TTY tty_1 (.data(ttydriver_1_data), .clk(CLK), .we(ttydriver_1_write));  // open: clr
  TTYDriver ttydriver_1 (
    .RXIN(pull_resistor_1_node), .CLK(CLK), .TTY_ADDR(in_2), .TXOUT(pull_resistor_1_node),
    .WRITE(ttydriver_1_write), .DATA(ttydriver_1_data));
  TTY tty_2 (.data(ttydriver_2_data), .clk(CLK), .we(ttydriver_2_write));  // open: clr
  TTYDriver ttydriver_2 (
    .RXIN(pull_resistor_1_node), .CLK(CLK), .TTY_ADDR(in_4), .TXOUT(pull_resistor_1_node),
    .WRITE(ttydriver_2_write), .DATA(ttydriver_2_data));
  TTY tty_3 (.data(ttydriver_3_data), .clk(CLK), .we(ttydriver_3_write));  // open: clr
  TTYDriver ttydriver_3 (
    .RXIN(pull_resistor_1_node), .CLK(CLK), .TTY_ADDR(in_5), .TXOUT(pull_resistor_1_node),
    .WRITE(ttydriver_3_write), .DATA(ttydriver_3_data));
  // Probe on vpwbmonitor_1_out_4
  // Probe on vpwbmonitor_1_last_fe
  // Probe on vpwbmonitor_1_last_addr
  // Probe on vpwbmonitor_1_last_data
endmodule

module KeyboardDriver (
  input  DR,
  input  [6:0] DATA,
  input  RXIN,
  input  [3:0] DEST,
  input  CLK,
  output TXOUT,
  output READ
);

  wire ADDR, and_1_out, CHKDR, CS, JUMP, O, or_1_out, txrxd_1_din, vpwbcontroller_1_ser_out, W;
  wire [5:5] rom_1_data;
  wire [7:0] NPC, PC, PCPLUS1, PCTARGET;
  wire [11:0] multiplexer_1_out;

  Register register_1 (.D(NPC), .en(1'b1), .clk(CLK), .Q(PC));  // open: clr
  Adder adder_1 (.a(8'h1), .b(PC), .out(PCPLUS1));  // open: cin, cout
  ROM #(.dataWidth(16)) rom_1 (.addr(PC), .data({PCTARGET, JUMP, CHKDR, rom_1_data[5], READ, ADDR, O, W, CS}));
  Multiplexer #(.width(12)) multiplexer_1 (.in0(12'h1), .in1({DEST, 1'b0, DATA}), .out(multiplexer_1_out), .sel(ADDR));
  VPWBController vpwbcontroller_1 (
    .O(O), .ADDR(ADDR), .DATAIN(multiplexer_1_out), .CS(CS), .W(W), .CLK(CLK), .SER_IN(txrxd_1_din),
    .SER_OUT(vpwbcontroller_1_ser_out));  // open: I, DATAOUT
  and and_1 (and_1_out, CHKDR, DR);
  or or_1 (or_1_out, and_1_out, JUMP);
  Multiplexer #(.width(8)) multiplexer_2 (.in0(PCPLUS1), .in1(PCTARGET), .out(NPC), .sel(or_1_out));
  TXRXD txrxd_1 (.DOUT(vpwbcontroller_1_ser_out), .RXIN(RXIN), .DIN(txrxd_1_din), .TXOUT(TXOUT));

  // Other names for the same wires on the sheet: DATA_t[6:0] = DATA

  // Notes on the sheet:
  //   contents of rom_1 (hex, n*v repeats v):
  //   7 4 7 547 387 1c 387
endmodule

module TTYDriver (
  input  RXIN,
  input  [3:0] TTY_ADDR,
  input  CLK,
  output [6:0] DATA,
  output TXOUT,
  output WRITE
);

  wire ADDR, and_1_out, CHKDR, comparator_1_eq, CS, DR, JUMP, not_1_out, O, or_1_out, txrxd_1_din,
       vpwbcontroller_1_ser_out, W, WRITE_TTY;
  wire [5:5] rom_1_data;
  wire [7:0] NPC, PC, PCPLUS1, PCTARGET;
  wire [11:0] DATAOUT, register_2_q;

  Register register_1 (.D(NPC), .en(1'b1), .clk(CLK), .Q(PC));  // open: clr
  Adder adder_1 (.a(8'h1), .b(PC), .out(PCPLUS1));  // open: cin, cout
  ROM #(.dataWidth(16)) rom_1 (.addr(PC), .data({PCTARGET, JUMP, CHKDR, rom_1_data[5], WRITE_TTY, ADDR, O, W, CS}));
  Register #(.width(12)) register_2 (
    .D(DATAOUT), .en(not_1_out), .clk(CLK), .Q({register_2_q[11:2], DR, register_2_q[0]}));  // open: clr
  not not_1 (not_1_out, O);
  and and_1 (and_1_out, CHKDR, DR);
  VPWBController vpwbcontroller_1 (
    .O(O), .ADDR(ADDR), .DATAIN({4'b1111, TTY_ADDR, 4'b0001}), .CS(CS), .W(W), .CLK(CLK),
    .SER_IN(txrxd_1_din), .DATAOUT(DATAOUT), .SER_OUT(vpwbcontroller_1_ser_out));  // open: I
  Multiplexer #(.width(8)) multiplexer_1 (.in0(PCPLUS1), .in1(PCTARGET), .out(NPC), .sel(or_1_out));
  or or_1 (or_1_out, and_1_out, JUMP);
  Comparator #(.mode("unsigned"), .width(4)) comparator_1 (
    .a(register_2_q[11:8]), .b(TTY_ADDR), .eq(comparator_1_eq));  // open: gt, lt
  and and_2 (WRITE, comparator_1_eq, WRITE_TTY);
  Multiplexer #(.width(7)) multiplexer_2 (
    .in0({7{1'b0}}), .in1({register_2_q[6:2], DR, register_2_q[0]}), .out(DATA), .sel(WRITE));
  TXRXD txrxd_1 (.DOUT(vpwbcontroller_1_ser_out), .RXIN(RXIN), .DIN(txrxd_1_din), .TXOUT(TXOUT));

  // Other names for the same wires on the sheet: CHAR[6:0] = DATA

  // Notes on the sheet:
  //   contents of rom_1 (hex, n*v repeats v):
  //   7 4 7 2 647 87 a 17 87
endmodule

module VPWBMonitor (
  input  RXIN,
  input  CLK,
  output [31:0] out_3,
  output [24:0] out_4,
  output LAST_FE,
  output [3:0] LAST_ADDR,
  output [7:0] LAST_DATA
);

  wire B0_ERR, B1_ERR, B2_ERR, B3_ERR, B4_ERR, B5_ERR, B6_ERR, B7_ERR, B8_ERR, B9_ERR, BA_ERR, BB_ERR,
       FOUND_IDLE, I4, I5, I6, I7, I8, I9, I10, I11, I12, I13, I14, I15, I16, I17, I18, I19, I20, I21, I22,
       I23, I24, I25, I26, I27, I28, I29, NEW_IDLE, not_7_out;
  wire [0:0] not_1_out, not_2_out, not_9_out, not_10_out, not_15_out, not_16_out, shifter_1_out_3,
       shifter_2_out_3, shifter_3_out_3, shifter_6_out_3, shifter_7_out_3, shifter_8_out_3, shifter_10_out_3,
       shifter_11_out_3, shifter_12_out_3;
  wire [1:0] shifter_1_out, shifter_2_out, shifter_3_out, shifter_6_out, shifter_7_out, shifter_8_out,
       shifter_10_out, shifter_11_out, shifter_12_out;
  wire [4:0] FRAME_LENGTH, priority_encoder_1_out;
  wire [5:0] subtractor_1_out, subtractor_2_out;
  wire [9:0] shifter_12_out_2;
  wire [10:0] shifter_11_out_2;
  wire [11:0] shifter_10_out_2, shifter_13_out;
  wire [13:0] shifter_8_out_2;
  wire [14:0] shifter_7_out_2;
  wire [15:0] shifter_6_out_2, shifter_9_out;
  wire [17:0] shifter_3_out_2;
  wire [18:0] shifter_2_out_2;
  wire [19:0] shifter_1_out_2, shifter_4_out;
  wire [24:0] and_6_out, not_8_out;
  wire [25:0] shifter_5_out;

  not not_1 (not_1_out[0], LAST_DATA[1]);
  not not_2 (not_2_out[0], LAST_DATA[3]);
  Subtractor #(.width(6)) subtractor_1 (
    .a(6'b011001), .b({1'b0, FRAME_LENGTH}), .out(subtractor_1_out));  // open: bin, bout
  Shifter #(.shift("lr"), .width(23)) shifter_1 (
    .in(out_4[24:2]), .\dist ({4'b0000, LAST_DATA[0]}),
    .out({shifter_1_out_2, shifter_1_out, shifter_1_out_3[0]}));
  Shifter #(.shift("lr"), .width(22)) shifter_2 (
    .in({shifter_1_out_2, shifter_1_out}), .\dist ({4'b0000, not_1_out[0]}),
    .out({shifter_2_out_2, shifter_2_out, shifter_2_out_3[0]}));
  Shifter #(.shift("lr"), .width(21)) shifter_3 (
    .in({shifter_2_out_2, shifter_2_out}), .\dist ({4'b0000, LAST_DATA[2]}),
    .out({shifter_3_out_2, shifter_3_out, shifter_3_out_3[0]}));
  Shifter #(.shift("lr"), .width(20)) shifter_4 (
    .in({shifter_3_out_2, shifter_3_out}), .\dist ({4'b0000, not_2_out[0]}), .out(shifter_4_out));
  // Probe on shifter_5_out
  and and_1 (B0_ERR, ~out_4[1], ~out_4[2], ~out_4[3]);  // AND_Gate
  not not_3 (LAST_DATA[0], out_4[2]);
  and and_2 (B1_ERR, shifter_1_out_3[0], shifter_1_out[0], shifter_1_out[1]);
  not not_4 (LAST_DATA[1], shifter_1_out[0]);
  and and_3 (B2_ERR, ~shifter_2_out_3[0], ~shifter_2_out[0], ~shifter_2_out[1]);  // AND_Gate
  not not_5 (LAST_DATA[2], shifter_2_out[0]);
  and and_4 (B3_ERR, shifter_3_out_3[0], shifter_3_out[0], shifter_3_out[1]);
  not not_6 (LAST_DATA[3], shifter_3_out[0]);
  not not_7 (not_7_out, RXIN);
  Shift_Register #(.length(32)) shift_register_1 (
    .shift(1'b1), .in(not_7_out), .clk(CLK), .out(out_3[31]), .q0(out_3[0]), .q1(out_3[1]), .q2(out_3[2]),
    .q3(out_3[3]), .q4(out_3[4]), .q5(out_3[5]), .q6(out_3[6]), .q7(out_3[7]), .q8(out_3[8]), .q9(out_3[9]),
    .q10(out_3[10]), .q11(out_3[11]), .q12(out_3[12]), .q13(out_3[13]), .q14(out_3[14]), .q15(out_3[15]),
    .q16(out_3[16]), .q17(out_3[17]), .q18(out_3[18]), .q19(out_3[19]), .q20(out_3[20]), .q21(out_3[21]),
    .q22(out_3[22]), .q23(out_3[23]), .q24(out_3[24]), .q25(out_3[25]), .q26(out_3[26]), .q27(out_3[27]),
    .q28(out_3[28]), .q29(out_3[29]), .q30(out_3[30]));  // open: load, clr, d0, d1, d2, d3, d4, d5, d6, d7, d8, d9, d10, d11, d12, d13, d14, d15, d16, d17, d18, d19, d20, d21, d22, d23, d24, d25, d26, d27, d28, d29, d30, d31, q31
  and and_5 (NEW_IDLE, ~out_3[0], ~out_3[1], ~out_3[2], out_3[3]);  // AND_Gate
  assign not_8_out = ~shifter_5_out[24:0];  // NOT_Gate not_8, 25 bits wide
  Shifter #(.shift("ar"), .width(26)) shifter_5 (.in(26'h2000000), .\dist (subtractor_1_out[4:0]), .out(shifter_5_out));
  not not_9 (not_9_out[0], LAST_DATA[5]);
  not not_10 (not_10_out[0], LAST_DATA[7]);
  Shifter #(.shift("lr"), .width(19)) shifter_6 (
    .in(shifter_4_out[19:1]), .\dist ({4'b0000, LAST_DATA[4]}),
    .out({shifter_6_out_2, shifter_6_out, shifter_6_out_3[0]}));
  Shifter #(.shift("lr"), .width(18)) shifter_7 (
    .in({shifter_6_out_2, shifter_6_out}), .\dist ({4'b0000, not_9_out[0]}),
    .out({shifter_7_out_2, shifter_7_out, shifter_7_out_3[0]}));
  Shifter #(.shift("lr"), .width(17)) shifter_8 (
    .in({shifter_7_out_2, shifter_7_out}), .\dist ({4'b0000, LAST_DATA[6]}),
    .out({shifter_8_out_2, shifter_8_out, shifter_8_out_3[0]}));
  Shifter #(.shift("lr"), .width(16)) shifter_9 (
    .in({shifter_8_out_2, shifter_8_out}), .\dist ({3'b000, not_10_out[0]}), .out(shifter_9_out));
  // Probe on and_6_out
  Register #(.width(25)) register_1 (.D(and_6_out), .en(NEW_IDLE), .clk(CLK), .Q(out_4));  // open: clr
  assign and_6_out = out_3[27:3] & not_8_out;  // AND_Gate and_6, 25 bits wide
  and and_7 (B4_ERR, ~shifter_4_out[0], ~shifter_4_out[1], ~shifter_4_out[2]);  // AND_Gate
  not not_11 (LAST_DATA[4], shifter_4_out[1]);
  and and_8 (B5_ERR, shifter_6_out_3[0], shifter_6_out[0], shifter_6_out[1]);
  not not_12 (LAST_DATA[5], shifter_6_out[0]);
  and and_9 (B6_ERR, ~shifter_7_out_3[0], ~shifter_7_out[0], ~shifter_7_out[1]);  // AND_Gate
  not not_13 (LAST_DATA[6], shifter_7_out[0]);
  and and_10 (B7_ERR, shifter_8_out_3[0], shifter_8_out[0], shifter_8_out[1]);
  not not_14 (LAST_DATA[7], shifter_8_out[0]);
  not not_15 (not_15_out[0], LAST_ADDR[1]);
  not not_16 (not_16_out[0], LAST_ADDR[3]);
  and and_11 (B8_ERR, ~shifter_9_out[0], ~shifter_9_out[1], ~shifter_9_out[2]);  // AND_Gate
  not not_17 (LAST_ADDR[0], shifter_9_out[1]);
  Shifter #(.shift("lr"), .width(15)) shifter_10 (
    .in(shifter_9_out[15:1]), .\dist ({3'b000, LAST_ADDR[0]}),
    .out({shifter_10_out_2, shifter_10_out, shifter_10_out_3[0]}));
  and and_12 (B9_ERR, shifter_10_out_3[0], shifter_10_out[0], shifter_10_out[1]);
  not not_18 (LAST_ADDR[1], shifter_10_out[0]);
  Shifter #(.shift("lr"), .width(14)) shifter_11 (
    .in({shifter_10_out_2, shifter_10_out}), .\dist ({3'b000, not_15_out[0]}),
    .out({shifter_11_out_2, shifter_11_out, shifter_11_out_3[0]}));
  and and_13 (BA_ERR, ~shifter_11_out_3[0], ~shifter_11_out[0], ~shifter_11_out[1]);  // AND_Gate
  not not_19 (LAST_ADDR[2], shifter_11_out[0]);
  Shifter #(.shift("lr"), .width(13)) shifter_12 (
    .in({shifter_11_out_2, shifter_11_out}), .\dist ({3'b000, LAST_ADDR[2]}),
    .out({shifter_12_out_2, shifter_12_out, shifter_12_out_3[0]}));
  and and_14 (BB_ERR, shifter_12_out_3[0], shifter_12_out[0], shifter_12_out[1]);
  not not_20 (LAST_ADDR[3], shifter_12_out[0]);
  Shifter #(.shift("lr"), .width(12)) shifter_13 (
    .in({shifter_12_out_2, shifter_12_out}), .\dist ({3'b000, not_16_out[0]}), .out(shifter_13_out));
  and and_15 (I29, ~out_3[31], ~out_3[30], ~out_3[29]);  // AND_Gate
  and and_16 (I28, ~out_3[30], ~out_3[29], ~out_3[28]);  // AND_Gate
  and and_17 (I27, ~out_3[29], ~out_3[28], ~out_3[27]);  // AND_Gate
  and and_18 (I26, ~out_3[28], ~out_3[27], ~out_3[26]);  // AND_Gate
  and and_19 (I24, ~out_3[26], ~out_3[25], ~out_3[24]);  // AND_Gate
  and and_20 (I23, ~out_3[25], ~out_3[24], ~out_3[23]);  // AND_Gate
  and and_21 (I25, ~out_3[27], ~out_3[26], ~out_3[25]);  // AND_Gate
  or or_1 (LAST_FE, out_4[1], B0_ERR, B1_ERR, B2_ERR, B3_ERR, B4_ERR, B5_ERR, B6_ERR, B7_ERR, B8_ERR, B9_ERR, BA_ERR, BB_ERR);
  and and_22 (I22, ~out_3[24], ~out_3[23], ~out_3[22]);  // AND_Gate
  and and_23 (I21, ~out_3[23], ~out_3[22], ~out_3[21]);  // AND_Gate
  and and_24 (I20, ~out_3[22], ~out_3[21], ~out_3[20]);  // AND_Gate
  and and_25 (I19, ~out_3[21], ~out_3[20], ~out_3[19]);  // AND_Gate
  and and_26 (I18, ~out_3[20], ~out_3[19], ~out_3[18]);  // AND_Gate
  and and_27 (I17, ~out_3[19], ~out_3[18], ~out_3[17]);  // AND_Gate
  and and_28 (I16, ~out_3[18], ~out_3[17], ~out_3[16]);  // AND_Gate
  and and_29 (I15, ~out_3[17], ~out_3[16], ~out_3[15]);  // AND_Gate
  and and_30 (I14, ~out_3[16], ~out_3[15], ~out_3[14]);  // AND_Gate
  and and_31 (I13, ~out_3[15], ~out_3[14], ~out_3[13]);  // AND_Gate
  and and_32 (I12, ~out_3[14], ~out_3[13], ~out_3[12]);  // AND_Gate
  and and_33 (I11, ~out_3[13], ~out_3[12], ~out_3[11]);  // AND_Gate
  and and_34 (I10, ~out_3[12], ~out_3[11], ~out_3[10]);  // AND_Gate
  and and_35 (I9, ~out_3[11], ~out_3[10], ~out_3[9]);  // AND_Gate
  and and_36 (I8, ~out_3[10], ~out_3[9], ~out_3[8]);  // AND_Gate
  and and_37 (I7, ~out_3[9], ~out_3[8], ~out_3[7]);  // AND_Gate
  and and_38 (I6, ~out_3[8], ~out_3[7], ~out_3[6]);  // AND_Gate
  and and_39 (I5, ~out_3[7], ~out_3[6], ~out_3[5]);  // AND_Gate
  and and_40 (I4, ~out_3[6], ~out_3[5], ~out_3[4]);  // AND_Gate
  Priority_Encoder #(.select(5)) priority_encoder_1 (
    .in0(I29), .in1(I28), .in2(I27), .in3(I26), .in4(I25), .in5(I24), .in6(I23), .in7(I22), .in8(I21),
    .in9(I20), .in10(I19), .in11(I18), .in12(I17), .in13(I16), .in14(I15), .in15(I14), .in16(I13),
    .in17(I12), .in18(I11), .in19(I10), .in20(I9), .in21(I8), .in22(I7), .in23(I6), .in24(I5), .in25(I4),
    .in26(1'b0), .in27(1'b0), .in28(1'b0), .in29(1'b0), .in30(1'b0), .in31(1'b0),
    .out(priority_encoder_1_out), .gs(FOUND_IDLE));  // open: en_out, en_in
  Subtractor #(.width(6)) subtractor_2 (
    .a(6'b011010), .b({1'b0, priority_encoder_1_out}), .out(subtractor_2_out));  // open: bin, bout
  Multiplexer #(.width(5)) multiplexer_1 (
    .in0({5{1'b0}}), .in1(subtractor_2_out[4:0]), .out(FRAME_LENGTH), .sel(FOUND_IDLE));

  // Other names for the same wires on the sheet: LAST_FRAME[24:0] = out_4; HIST[31:0] = out_3; B8 = LAST_ADDR[0];
  //   B9 = LAST_ADDR[1]; BA = LAST_ADDR[2]; BB = LAST_ADDR[3]; B0 = LAST_DATA[0]; B1 = LAST_DATA[1];
  //   B2 = LAST_DATA[2]; B3 = LAST_DATA[3]; B4 = LAST_DATA[4]; B5 = LAST_DATA[5]; B6 = LAST_DATA[6];
  //   B7 = LAST_DATA[7]; EOF_ERR = out_4[1]
endmodule

module TXRXD (
  input  DOUT,
  input  RXIN,
  output TXOUT,
  output DIN
);

  assign TXOUT = DOUT ? ~DOUT : 1'bz;  // Controlled_Inverter controlled_inverter_1
  not not_1 (DIN, RXIN);

  // Notes on the sheet:
  //   TXOUT: pull=down
endmodule

module VPWBController (
  input  CS,
  input  W,
  input  SER_IN,
  input  O,
  input  ADDR,
  input  [11:0] DATAIN,
  input  CLK,
  output SER_OUT,
  output I,
  output [11:0] DATAOUT
);
endmodule

module VPWBTX (
  input  [11:0] FRAME_IN,
  input  SER_IN,
  input  WRITE,
  input  ENA,
  input  CLK,
  output SER_OUT,
  output FULL,
  output IDLE
);
endmodule

module VPWBRX (
  input  [3:0] CARE,
  input  [3:0] ADDR,
  input  SER_IN,
  input  READ,
  input  ENA,
  input  CLK,
  output [11:0] FRAME_OUT,
  output FULL,
  output EMPTY,
  output [11:0] out_10
);

  wire not_1_out, OBSERVER_DIN, OBSERVER_IDLE, OBSERVER_NEWBIT, SRI_FULL, SRI_READ;

  not not_1 (not_1_out, FULL);
  and and_1 (SRI_READ, SRI_FULL, not_1_out);
  VPWBObserver vpwbobserver_1 (
    .ENA(ENA), .CLK(CLK), .RX(SER_IN), .DIN(OBSERVER_DIN), .NEWBIT(OBSERVER_NEWBIT), .IDLE(OBSERVER_IDLE));
  LED led_1 (.in(OBSERVER_DIN));
  LED led_2 (.in(OBSERVER_NEWBIT));
  LED led_3 (.in(OBSERVER_IDLE));
  VPWBSRI vpwbsri_1 (
    .READ(SRI_READ), .ENA(ENA), .CLK(CLK), .SER_IN(OBSERVER_DIN), .NEWBIT(OBSERVER_NEWBIT),
    .CLEAR(OBSERVER_IDLE), .FULL(SRI_FULL), .PARA_OUT(out_10));
  VPWBFrameQueue vpwbframequeue_1 (
    .FRAME_IN(out_10), .ENQUEUE(SRI_READ), .ENA(ENA), .CLK(CLK), .DEQUEUE(READ), .FULL(FULL),
    .FRAME_OUT(FRAME_OUT), .EMPTY(EMPTY));

  // Other names for the same wires on the sheet: SRI_PARA_OUT[11:0] = out_10
endmodule

module VPWBFrameQueue (
  input  [11:0] FRAME_IN,
  input  ENQUEUE,
  input  DEQUEUE,
  input  ENA,
  input  CLK,
  output [11:0] FRAME_OUT,
  output FULL,
  output EMPTY
);

  wire ADD, ADD_FROM_EMPTY, ADD_FROM_ONE, ADD_FROM_THREE, ADD_FROM_TWO, COUNT_FROM_FULL, COUNT_FROM_ONE_a,
       COUNT_FROM_THREE_a, COUNT_FROM_TWO_a, COUNT_ONE, COUNT_THREE, COUNT_TWO, FRAME_OUT_SELECT,
       HEAD_DATA_SELECT_S0_FROM_FULL_a, HEAD_DATA_SELECT_S0_FROM_THREE_a, HEAD_DATA_SELECT_S0_FROM_TWO_a,
       HEAD_WE, HEAD_WE_FROM_ONE_a, not_1_out, not_2_out, not_3_out, not_4_out, not_5_out, not_6_out,
       not_7_out, not_8_out, not_9_out, not_10_out, not_11_out, not_12_out, not_13_out, ONE_WE,
       QUEUE_COUNT_ENABLE, TAIL_WE, TWO_WE;
  wire [1:0] HEAD_DATA_SELECT, ONE_DATA_SELECT, TAIL_DATA_SELECT, TWO_DATA_SELECT;
  wire [2:0] COUNT_OUT;
  wire [11:0] QUEUE_HEAD_IN, QUEUE_ONE_IN, QUEUE_ONE_OUT, QUEUE_TAIL_IN, QUEUE_TAIL_OUT, QUEUE_TWO_IN,
       QUEUE_TWO_OUT, register_4_q;

  not not_1 (not_1_out, DEQUEUE);
  not not_2 (not_2_out, DEQUEUE);
  not not_3 (not_3_out, ENQUEUE);
  not not_4 (not_4_out, DEQUEUE);
  not not_5 (not_5_out, ENQUEUE);
  not not_6 (not_6_out, DEQUEUE);
  not not_7 (not_7_out, ENQUEUE);
  not not_8 (not_8_out, ENQUEUE);
  Demultiplexer #(.select(3)) demultiplexer_1 (
    .out0(EMPTY), .out1(COUNT_ONE), .out2(COUNT_TWO), .out3(COUNT_THREE), .out4(FULL), .in(1'b1),
    .sel(COUNT_OUT));  // open: out5, out6, out7
  and and_1 (ADD_FROM_EMPTY, EMPTY, ENQUEUE, not_1_out);
  and and_2 (FRAME_OUT_SELECT, EMPTY, ENQUEUE, DEQUEUE);
  Register #(.width(12)) register_1 (.D(QUEUE_TAIL_IN), .en(TAIL_WE), .clk(CLK), .Q(QUEUE_TAIL_OUT), .clr(not_9_out));
  not not_9 (not_9_out, ENA);
  Multiplexer #(.select(2), .width(12)) multiplexer_1 (
    .in0(FRAME_IN), .in2({12{1'b0}}), .out(QUEUE_TAIL_IN), .sel(TAIL_DATA_SELECT));  // open: in1, in3
  Multiplexer #(.select(2), .width(12)) multiplexer_2 (
    .in0(QUEUE_TAIL_OUT), .in1(FRAME_IN), .in2({12{1'b0}}), .out(QUEUE_ONE_IN), .sel(ONE_DATA_SELECT));  // open: in3
  and and_3 (ADD_FROM_ONE, COUNT_ONE, ENQUEUE, not_2_out);
  and and_4 (COUNT_FROM_ONE_a, COUNT_ONE, DEQUEUE, not_3_out);
  and and_5 (HEAD_WE_FROM_ONE_a, COUNT_ONE, DEQUEUE, ENQUEUE);
  and and_6 (ADD_FROM_TWO, COUNT_TWO, ENQUEUE, not_4_out);
  and and_7 (COUNT_FROM_TWO_a, COUNT_TWO, not_5_out, DEQUEUE);
  and and_8 (HEAD_DATA_SELECT_S0_FROM_TWO_a, COUNT_TWO, ENQUEUE, DEQUEUE);
  and and_9 (ADD_FROM_THREE, COUNT_THREE, ENQUEUE, not_6_out);
  and and_10 (COUNT_FROM_THREE_a, COUNT_THREE, not_7_out, DEQUEUE);
  and and_11 (HEAD_DATA_SELECT_S0_FROM_THREE_a, COUNT_THREE, ENQUEUE, DEQUEUE);
  and and_12 (COUNT_FROM_FULL, FULL, not_8_out, DEQUEUE);
  and and_13 (HEAD_DATA_SELECT_S0_FROM_FULL_a, FULL, ENQUEUE, DEQUEUE);
  not not_10 (not_10_out, ENA);
  or or_1 (TAIL_WE, ADD_FROM_THREE, COUNT_FROM_FULL, HEAD_DATA_SELECT_S0_FROM_FULL_a);
  or or_2 (ONE_WE, ADD_FROM_TWO, COUNT_FROM_THREE_a, HEAD_DATA_SELECT_S0_FROM_THREE_a, COUNT_FROM_FULL, HEAD_DATA_SELECT_S0_FROM_FULL_a);
  Counter #(.max('h7), .width(3)) counter_1 (
    .clr(not_10_out), .up(ADD), .count(QUEUE_COUNT_ENABLE), .clk(CLK), .Q(COUNT_OUT));  // open: load, D, carry
  Register #(.width(12)) register_2 (.D(QUEUE_ONE_IN), .en(ONE_WE), .clk(CLK), .Q(QUEUE_ONE_OUT), .clr(not_11_out));
  not not_11 (not_11_out, ENA);
  Multiplexer #(.select(2), .width(12)) multiplexer_3 (
    .in0(QUEUE_ONE_OUT), .in1(FRAME_IN), .in2({12{1'b0}}), .out(QUEUE_TWO_IN), .sel(TWO_DATA_SELECT));  // open: in3
  Multiplexer #(.select(2), .width(12)) multiplexer_4 (
    .in0(FRAME_IN), .in1(QUEUE_TWO_OUT), .in2({12{1'b0}}), .out(QUEUE_HEAD_IN), .sel(HEAD_DATA_SELECT));  // open: in3
  or or_3 (ADD, ADD_FROM_EMPTY, ADD_FROM_ONE, ADD_FROM_TWO, ADD_FROM_THREE);
  or or_4 (TWO_WE, ADD_FROM_ONE, COUNT_FROM_TWO_a, HEAD_DATA_SELECT_S0_FROM_TWO_a, COUNT_FROM_THREE_a, HEAD_DATA_SELECT_S0_FROM_THREE_a, COUNT_FROM_FULL, HEAD_DATA_SELECT_S0_FROM_FULL_a);
  or or_5 (HEAD_WE, ADD_FROM_EMPTY, COUNT_FROM_ONE_a, HEAD_WE_FROM_ONE_a, COUNT_FROM_TWO_a, HEAD_DATA_SELECT_S0_FROM_TWO_a, COUNT_FROM_THREE_a, HEAD_DATA_SELECT_S0_FROM_THREE_a, COUNT_FROM_FULL, HEAD_DATA_SELECT_S0_FROM_FULL_a);
  Register #(.width(12)) register_3 (.D(QUEUE_TWO_IN), .en(TWO_WE), .clk(CLK), .Q(QUEUE_TWO_OUT), .clr(not_12_out));
  not not_12 (not_12_out, ENA);
  Register #(.width(12)) register_4 (.D(QUEUE_HEAD_IN), .en(HEAD_WE), .clk(CLK), .Q(register_4_q), .clr(not_13_out));
  not not_13 (not_13_out, ENA);
  Register #(.trigger("high"), .width(12)) register_5 (.D(QUEUE_HEAD_IN), .en(1'b1), .clk(1'b1));  // open: Q, clr
  or or_6 (QUEUE_COUNT_ENABLE, ADD_FROM_EMPTY, ADD_FROM_ONE, COUNT_FROM_ONE_a, ADD_FROM_TWO, COUNT_FROM_TWO_a, ADD_FROM_THREE, COUNT_FROM_THREE_a, COUNT_FROM_FULL);
  buf or_7 (TAIL_DATA_SELECT[0], 1'b0);  // OR_Gate
  buf or_8 (TAIL_DATA_SELECT[1], COUNT_FROM_FULL);  // OR_Gate
  Multiplexer #(.width(12)) multiplexer_5 (.in0(register_4_q), .in1(FRAME_IN), .out(FRAME_OUT), .sel(FRAME_OUT_SELECT));
  or or_9 (ONE_DATA_SELECT[0], ADD_FROM_TWO, HEAD_DATA_SELECT_S0_FROM_THREE_a);
  buf or_10 (ONE_DATA_SELECT[1], COUNT_FROM_THREE_a);  // OR_Gate
  or or_11 (TWO_DATA_SELECT[0], ADD_FROM_ONE, HEAD_DATA_SELECT_S0_FROM_TWO_a);
  buf or_12 (TWO_DATA_SELECT[1], COUNT_FROM_TWO_a);  // OR_Gate
  or or_13 (HEAD_DATA_SELECT[0], COUNT_FROM_TWO_a, HEAD_DATA_SELECT_S0_FROM_TWO_a, COUNT_FROM_THREE_a, HEAD_DATA_SELECT_S0_FROM_THREE_a, COUNT_FROM_FULL, HEAD_DATA_SELECT_S0_FROM_FULL_a);
  buf or_14 (HEAD_DATA_SELECT[1], COUNT_FROM_ONE_a);  // OR_Gate

  // Other names for the same wires on the sheet: COUNT_FROM_EMPTY = ADD_FROM_EMPTY;
  //   HEAD_WE_FROM_EMPTY = ADD_FROM_EMPTY; HEAD_DATA_SELECT_S1_FROM_ONE = COUNT_FROM_ONE_a;
  //   HEAD_WE_FROM_ONE = COUNT_FROM_ONE_a; COUNT_FROM_TWO = ADD_FROM_TWO; ONE_DATA_SELECT_S0_FROM_TWO = ADD_FROM_TWO;
  //   ONE_WE_FROM_TWO = ADD_FROM_TWO; COUNT_FROM_THREE = ADD_FROM_THREE; TAIL_WE_FROM_THREE = ADD_FROM_THREE;
  //   HEAD_DATA_SELECT_S0_FROM_FULL = COUNT_FROM_FULL; HEAD_WE_FROM_FULL = COUNT_FROM_FULL;
  //   ONE_WE_FROM_FULL = COUNT_FROM_FULL; TAIL_DATA_SELECT_S1_FROM_FULL = COUNT_FROM_FULL;
  //   TAIL_WE_FROM_FULL = COUNT_FROM_FULL; TWO_WE_FROM_FULL = COUNT_FROM_FULL;
  //   HEAD_WE_FROM_FULL_a = HEAD_DATA_SELECT_S0_FROM_FULL_a; ONE_WE_FROM_FULL_a = HEAD_DATA_SELECT_S0_FROM_FULL_a;
  //   TAIL_WE_FROM_FULL_a = HEAD_DATA_SELECT_S0_FROM_FULL_a; TWO_WE_FROM_FULL_a = HEAD_DATA_SELECT_S0_FROM_FULL_a;
  //   COUNT_FROM_ONE = ADD_FROM_ONE; TWO_DATA_SELECT_S0_FROM_ONE = ADD_FROM_ONE; TWO_WE_FROM_ONE = ADD_FROM_ONE;
  //   HEAD_DATA_SELECT_S0_FROM_THREE = COUNT_FROM_THREE_a; HEAD_WE_FROM_THREE = COUNT_FROM_THREE_a;
  //   ONE_DATA_SELECT_S1_FROM_THREE = COUNT_FROM_THREE_a; ONE_WE_FROM_THREE = COUNT_FROM_THREE_a;
  //   TWO_WE_FROM_THREE = COUNT_FROM_THREE_a; HEAD_WE_FROM_THREE_a = HEAD_DATA_SELECT_S0_FROM_THREE_a;
  //   ONE_DATA_SELECT_S0_FROM_THREE = HEAD_DATA_SELECT_S0_FROM_THREE_a;
  //   ONE_WE_FROM_THREE_a = HEAD_DATA_SELECT_S0_FROM_THREE_a; TWO_WE_FROM_THREE_a = HEAD_DATA_SELECT_S0_FROM_THREE_a;
  //   HEAD_DATA_SELECT_S0_FROM_TWO = COUNT_FROM_TWO_a; HEAD_WE_FROM_TWO = COUNT_FROM_TWO_a;
  //   TWO_DATA_SELECT_S1_FROM_TWO = COUNT_FROM_TWO_a; TWO_WE_FROM_TWO = COUNT_FROM_TWO_a;
  //   HEAD_WE_FROM_TWO_a = HEAD_DATA_SELECT_S0_FROM_TWO_a;
  //   TWO_DATA_SELECT_S0_FROM_TWO = HEAD_DATA_SELECT_S0_FROM_TWO_a;
  //   TWO_WE_FROM_TWO_a = HEAD_DATA_SELECT_S0_FROM_TWO_a
endmodule

module VPWBSRI (
  input  READ,
  input  SER_IN,
  input  NEWBIT,
  input  CLEAR,
  input  ENA,
  input  CLK,
  output FULL,
  output [11:0] PARA_OUT
);

  wire and_1_out, and_2_out, CLEAR_REG_AND_COUNT, not_1_out, not_2_out, not_3_out, SRI_REG_OUT_FRAMEBIT;
  wire [3:0] SRI_COUNTER_OUT;
  wire [11:0] SRI_REG_OUT;

  not not_1 (not_1_out, ENA);
  and and_1 (and_1_out, FULL, READ);
  or or_1 (CLEAR_REG_AND_COUNT, and_1_out, CLEAR);
  // Shift_Register #(.length(13)) shift_register_1: pin names not known; wires that end beside it: not_1_out, CLEAR_REG_AND_COUNT, NEWBIT, CLK, SER_IN, 1'b0, 1'b0, 1'b0, 1'b0, 1'b0, 1'b0, 1'b0, 1'b0, 1'b0, 1'b0, 1'b0, 1'b0, SRI_REG_OUT_FRAMEBIT, SRI_REG_OUT[0], SRI_REG_OUT[1], SRI_REG_OUT[2], SRI_REG_OUT[3], SRI_REG_OUT[4], SRI_REG_OUT[5], SRI_REG_OUT[6], SRI_REG_OUT[7], SRI_REG_OUT[8], SRI_REG_OUT[9], SRI_REG_OUT[10]
  Multiplexer #(.width(12)) multiplexer_1 (.in0({12{1'b0}}), .in1(SRI_REG_OUT), .out(PARA_OUT), .sel(and_2_out));
  and and_2 (and_2_out, FULL, SRI_REG_OUT_FRAMEBIT);
  not not_2 (not_2_out, ENA);
  Counter #(.max('hf), .width(4)) counter_1 (
    .clr(not_2_out), .load(CLEAR_REG_AND_COUNT), .up(1'b1), .count(NEWBIT), .clk(CLK), .D(4'b0000),
    .Q(SRI_COUNTER_OUT));  // open: carry
  not not_3 (not_3_out, SRI_COUNTER_OUT[1]);
  and and_3 (FULL, SRI_COUNTER_OUT[0], not_3_out, SRI_COUNTER_OUT[2], SRI_COUNTER_OUT[3]);

  // Other names for the same wires on the sheet: SRI_REG_OUT_0 = SRI_REG_OUT[0]; SRI_REG_OUT_1 = SRI_REG_OUT[1];
  //   SRI_REG_OUT_2 = SRI_REG_OUT[2]; SRI_REG_OUT_3 = SRI_REG_OUT[3]; SRI_REG_OUT_4 = SRI_REG_OUT[4];
  //   SRI_REG_OUT_5 = SRI_REG_OUT[5]; SRI_REG_OUT_6 = SRI_REG_OUT[6]; SRI_REG_OUT_7 = SRI_REG_OUT[7];
  //   SRI_REG_OUT_8 = SRI_REG_OUT[8]; SRI_REG_OUT_9 = SRI_REG_OUT[9]; SRI_REG_OUT_10 = SRI_REG_OUT[10];
  //   SRI_REG_OUT_11 = SRI_REG_OUT[11]
endmodule

module VPWBSRO (
  input  [11:0] PARA_IN,
  input  LOAD,
  input  SHIFT,
  input  RELOAD,
  input  ENA,
  input  CLK,
  output SER_OUT,
  output EMPTY,
  output [3:0] BITSLEFT
);

  wire and_3_out, EMPTY_ALL_1, EMPTY_END, EMPTY_START, LOAD_IN, not_1_out, not_2_out, not_3_out, not_4_out,
       not_5_out, not_6_out, not_7_out, not_8_out, not_9_out, not_10_out, not_11_out, not_12_out, not_13_out,
       not_14_out, not_15_out, not_16_out, not_17_out, not_18_out, not_19_out, SHIFT_REG_0_IN,
       SHIFT_REG_0_OUT, SHIFT_REG_1_IN, SHIFT_REG_1_OUT, SHIFT_REG_2_IN, SHIFT_REG_2_OUT, SHIFT_REG_3_IN,
       SHIFT_REG_3_OUT, SHIFT_REG_4_IN, SHIFT_REG_4_OUT, SHIFT_REG_5_IN, SHIFT_REG_5_OUT, SHIFT_REG_6_IN,
       SHIFT_REG_6_OUT, SHIFT_REG_7_IN, SHIFT_REG_7_OUT, SHIFT_REG_8_IN, SHIFT_REG_8_OUT, SHIFT_REG_9_IN,
       SHIFT_REG_9_OUT, SHIFT_REG_10_IN, SHIFT_REG_10_OUT, SHIFT_REG_11_IN;
  wire [11:0] BUFF_REG_OUT;

  Multiplexer multiplexer_1 (.in0(PARA_IN[0]), .in1(BUFF_REG_OUT[0]), .out(SHIFT_REG_0_IN), .sel(RELOAD));
  Multiplexer multiplexer_2 (.in0(PARA_IN[1]), .in1(BUFF_REG_OUT[1]), .out(SHIFT_REG_1_IN), .sel(RELOAD));
  Multiplexer multiplexer_3 (.in0(PARA_IN[2]), .in1(BUFF_REG_OUT[2]), .out(SHIFT_REG_2_IN), .sel(RELOAD));
  not not_1 (not_1_out, ENA);
  // Shift_Register #(.length(12)) shift_register_1: pin names not known; wires that end beside it: not_1_out, LOAD_IN, SHIFT, CLK, 1'b1, SHIFT_REG_0_IN, SHIFT_REG_1_IN, SHIFT_REG_2_IN, SHIFT_REG_3_IN, SHIFT_REG_4_IN, SHIFT_REG_5_IN, SHIFT_REG_6_IN, SHIFT_REG_7_IN, SHIFT_REG_8_IN, SHIFT_REG_9_IN, SHIFT_REG_10_IN, SHIFT_REG_11_IN, SHIFT_REG_0_OUT, SHIFT_REG_1_OUT, SHIFT_REG_2_OUT, SHIFT_REG_3_OUT, SHIFT_REG_4_OUT, SHIFT_REG_5_OUT, SHIFT_REG_6_OUT, SHIFT_REG_7_OUT, SHIFT_REG_8_OUT, SHIFT_REG_9_OUT, SHIFT_REG_10_OUT, SER_OUT
  or or_1 (LOAD_IN, LOAD, RELOAD);
  not not_2 (not_2_out, SHIFT_REG_0_OUT);
  not not_3 (not_3_out, SHIFT_REG_1_OUT);
  not not_4 (not_4_out, SHIFT_REG_2_OUT);
  not not_5 (not_5_out, SHIFT_REG_3_OUT);
  not not_6 (not_6_out, SHIFT_REG_4_OUT);
  not not_7 (not_7_out, SHIFT_REG_5_OUT);
  not not_8 (not_8_out, SHIFT_REG_6_OUT);
  not not_9 (not_9_out, SHIFT_REG_7_OUT);
  not not_10 (not_10_out, SHIFT_REG_8_OUT);
  not not_11 (not_11_out, SHIFT_REG_9_OUT);
  not not_12 (not_12_out, SHIFT_REG_10_OUT);
  not not_13 (not_13_out, SER_OUT);
  and and_1 (EMPTY_START, not_2_out, not_3_out, not_4_out, not_5_out, not_6_out, not_7_out, not_8_out, not_9_out, not_10_out, not_11_out, not_12_out, not_13_out);
  and and_2 (EMPTY_ALL_1, SHIFT_REG_0_OUT, SHIFT_REG_1_OUT, SHIFT_REG_2_OUT, SHIFT_REG_3_OUT, SHIFT_REG_4_OUT, SHIFT_REG_5_OUT, SHIFT_REG_6_OUT, SHIFT_REG_7_OUT, SHIFT_REG_8_OUT, SHIFT_REG_9_OUT, SHIFT_REG_10_OUT, SER_OUT);
  Multiplexer multiplexer_4 (.in0(PARA_IN[3]), .in1(BUFF_REG_OUT[3]), .out(SHIFT_REG_3_IN), .sel(RELOAD));
  Multiplexer multiplexer_5 (.in0(PARA_IN[4]), .in1(BUFF_REG_OUT[4]), .out(SHIFT_REG_4_IN), .sel(RELOAD));
  Multiplexer multiplexer_6 (.in0(PARA_IN[5]), .in1(BUFF_REG_OUT[5]), .out(SHIFT_REG_5_IN), .sel(RELOAD));
  not not_14 (not_14_out, BITSLEFT[0]);
  not not_15 (not_15_out, BITSLEFT[1]);
  not not_16 (not_16_out, BITSLEFT[2]);
  not not_17 (not_17_out, BITSLEFT[3]);
  or or_2 (EMPTY, EMPTY_START, EMPTY_END);
  and and_3 (and_3_out, not_14_out, not_15_out, not_16_out, not_17_out);
  and and_4 (EMPTY_END, and_3_out, EMPTY_ALL_1);
  not not_18 (not_18_out, ENA);
  Counter #(.max('hf), .ongoal("stay"), .width(4)) counter_1 (
    .clr(not_18_out), .load(LOAD_IN), .up(1'b0), .count(SHIFT), .clk(CLK), .D(4'b1101), .Q(BITSLEFT));  // open: carry
  Register #(.width(12)) register_1 (.D(PARA_IN), .en(LOAD), .clk(CLK), .Q(BUFF_REG_OUT), .clr(not_19_out));
  not not_19 (not_19_out, ENA);
  Multiplexer multiplexer_7 (.in0(PARA_IN[6]), .in1(BUFF_REG_OUT[6]), .out(SHIFT_REG_6_IN), .sel(RELOAD));
  Multiplexer multiplexer_8 (.in0(PARA_IN[7]), .in1(BUFF_REG_OUT[7]), .out(SHIFT_REG_7_IN), .sel(RELOAD));
  Multiplexer multiplexer_9 (.in0(PARA_IN[8]), .in1(BUFF_REG_OUT[8]), .out(SHIFT_REG_8_IN), .sel(RELOAD));
  Multiplexer multiplexer_10 (.in0(PARA_IN[9]), .in1(BUFF_REG_OUT[9]), .out(SHIFT_REG_9_IN), .sel(RELOAD));
  Multiplexer multiplexer_11 (.in0(PARA_IN[10]), .in1(BUFF_REG_OUT[10]), .out(SHIFT_REG_10_IN), .sel(RELOAD));
  Multiplexer multiplexer_12 (.in0(PARA_IN[11]), .in1(BUFF_REG_OUT[11]), .out(SHIFT_REG_11_IN), .sel(RELOAD));

  // Other names for the same wires on the sheet: BUFFER_REG_OUT_BIT_0 = BUFF_REG_OUT[0];
  //   BUFFER_REG_OUT_BIT_1 = BUFF_REG_OUT[1]; BUFFER_REG_OUT_BIT_2 = BUFF_REG_OUT[2];
  //   BUFFER_REG_OUT_BIT_3 = BUFF_REG_OUT[3]; BUFFER_REG_OUT_BIT_4 = BUFF_REG_OUT[4];
  //   BUFFER_REG_OUT_BIT_5 = BUFF_REG_OUT[5]; BUFFER_REG_OUT_BIT_6 = BUFF_REG_OUT[6];
  //   BUFFER_REG_OUT_BIT_7 = BUFF_REG_OUT[7]; BUFFER_REG_OUT_BIT_8 = BUFF_REG_OUT[8];
  //   BUFFER_REG_OUT_BIT_9 = BUFF_REG_OUT[9]; BUFFER_REG_OUT_BIT_10 = BUFF_REG_OUT[10];
  //   BUFFER_REG_OUT_BIT_11 = BUFF_REG_OUT[11]; PARA_IN_BIT_0 = PARA_IN[0]; PARA_IN_BIT_1 = PARA_IN[1];
  //   PARA_IN_BIT_2 = PARA_IN[2]; PARA_IN_BIT_3 = PARA_IN[3]; PARA_IN_BIT_4 = PARA_IN[4]; PARA_IN_BIT_5 = PARA_IN[5];
  //   PARA_IN_BIT_6 = PARA_IN[6]; PARA_IN_BIT_7 = PARA_IN[7]; PARA_IN_BIT_8 = PARA_IN[8]; PARA_IN_BIT_9 = PARA_IN[9];
  //   PARA_IN_BIT_10 = PARA_IN[10]; PARA_IN_BIT_11 = PARA_IN[11]; SHIFT_REG_11_OUT = SER_OUT
endmodule

module VPWBArbiter (
  input  EVENBIT,
  input  DOUT,
  input  DW,
  input  RX,
  input  ENA,
  input  CLK,
  output TX,
  output ARBL,
  output BITCMP
);

  wire and_15_out, ARB_S0_RESET, ARB_S0_RESET_FROM_BIT1, ARB_S0_RESET_FROM_BIT1_a, ARB_S0_SET,
       ARB_S0_SET_FROM_BIT2, ARB_S0_SET_FROM_IDLE, ARB_S1_RESET, ARB_S1_RESET_FROM_BIT2, ARB_S1_SET,
       ARB_STATE_0_BIT, ARB_STATE_1_BIT, ARBL_LOSS_BIT1, ARBL_LOSS_BIT1_1, ARBL_LOSS_BIT2, ARBL_LOSS_BIT2_1,
       BIT1, BIT1_2, BIT1_STATE, BIT2, BIT2_2, BIT2_STATE, BITCMP_c, BITCMP_d, BITCOMP_TO_BIT1,
       BITCOMP_TO_IDLE, BITCOMPS, d_ff_4_q, d_ff_5_q, DW_0, IDLE_STATE, LONG, LONG_0, LONG_RESET, LONG_STATE,
       LONGSAVED, LONGSAVED_DISABLED, LONGSAVED_RESET, LOSS_B1, LOSS_B2, not_2_out, not_3_out, not_4_out,
       not_5_out, not_6_out, not_7_out, not_9_out, not_11_out, not_13_out, not_14_out, not_15_out,
       not_16_out, not_17_out, NOT_LONG_SAVED, NOT_LONG_STATE, NOTLONGSAVED_DISABLED, NOTLONGSAVED_RESET,
       ONECYCLE_COMPLETED, or_1_out, or_4_out, or_5_out, or_9_out, or_19_out, or_21_out, TO_IDLE, TO_RESET,
       TRANSMIT_DATA_BIT1, TRANSMITTING_DATA_IN_BIT2, TX1, TX2, xnor_1_out, xor_1_out, xor_2_out;
  wire [0:0] and_19_out;

  xor xor_1 (xor_1_out, BIT1, BIT1_2);
  not not_1 (DW_0, DW);
  and and_1 (ARB_S0_RESET_FROM_BIT1, BIT1, DW_0, LONG_0);
  and and_2 (ARB_S0_RESET_FROM_BIT1_a, BIT1, LONG);
  and and_3 (BITCMP_d, BIT1, LONG_0);
  and and_4 (ARB_S1_RESET_FROM_BIT2, BIT2, DW_0);
  and and_5 (ARB_S0_SET_FROM_BIT2, BIT2, DW);
  D_Flip_Flop d_ff_1 (.D(ARBL), .clk(CLK), .Q(TO_RESET));  // open: Qn, preset, reset
  or or_1 (or_1_out, BIT2, BIT2_2);
  S_R_Flip_Flop s_r_ff_1 (
    .S(ARB_S1_SET), .R(ARB_S1_RESET), .clk(CLK), .Q(ARB_STATE_1_BIT), .reset(not_2_out));  // open: Qn, preset
  not not_2 (not_2_out, ENA);
  not not_3 (not_3_out, DW);
  or or_2 (ARB_S0_SET, ARB_S0_SET_FROM_IDLE, ARB_S0_SET_FROM_BIT2, 1'b0);
  and and_6 (ARB_S0_SET_FROM_IDLE, BITCMP_c, DW);
  LED ARBLOSS_IN_BIT1_STATE (.in(LOSS_B1));
  LED ARBLOSS_IN_BIT2_STATE (.in(LOSS_B2));
  not not_4 (not_4_out, TX);
  not not_5 (not_5_out, RX);
  xor xor_2 (xor_2_out, BITCMP_c, BIT2_STATE);
  and and_7 (BITCOMP_TO_BIT1, BITCOMPS, DW);
  or or_3 (ARB_S1_SET, ARB_S0_RESET_FROM_BIT1_a, BITCOMP_TO_BIT1, 1'b0);
  and and_8 (BITCOMP_TO_IDLE, BITCOMPS, not_3_out);
  LED IDLE (.in(IDLE_STATE));
  LED u_BIT1 (.in(BIT1_STATE));
  LED u_BIT2 (.in(BIT2_STATE));
  Register #(.trigger("falling"), .width(1)) register_1 (
    .D(LONG_STATE), .en(LONGSAVED_DISABLED), .clk(CLK), .Q(LONGSAVED), .clr(LONG_RESET));
  and and_9 (BIT2_STATE, LONGSAVED, or_1_out);
  Register #(.trigger("falling"), .width(1)) register_2 (
    .D(NOT_LONG_STATE), .en(NOTLONGSAVED_DISABLED), .clk(CLK), .Q(NOT_LONG_SAVED), .clr(LONG_RESET));
  or or_4 (or_4_out, ONECYCLE_COMPLETED, BITCOMP_TO_BIT1, IDLE_STATE);
  and and_10 (ARBL_LOSS_BIT1_1, TRANSMIT_DATA_BIT1, not_4_out, RX);
  and and_11 (ARBL_LOSS_BIT1, TRANSMIT_DATA_BIT1, TX, not_5_out);
  not not_6 (not_6_out, RX);
  not not_7 (not_7_out, TX);
  or or_5 (or_5_out, xor_1_out, BIT1_2);
  not not_8 (LONG_0, LONG);
  or or_6 (LONG_RESET, or_4_out, TO_RESET);
  and and_12 (ARBL_LOSS_BIT2, TRANSMITTING_DATA_IN_BIT2, TX, not_6_out);
  and and_13 (ARBL_LOSS_BIT2_1, not_7_out, RX, TRANSMITTING_DATA_IN_BIT2);
  and and_14 (IDLE_STATE, BITCMP_c, xor_2_out);
  not not_9 (not_9_out, BIT2_STATE);
  D_Flip_Flop d_ff_2 (.D(NOT_LONG_SAVED), .clk(CLK), .Q(TRANSMIT_DATA_BIT1), .reset(TO_IDLE));  // open: Qn, preset
  S_R_Flip_Flop s_r_ff_2 (.S(EVENBIT), .R(1'b0), .clk(d_ff_4_q), .Q(TX2), .reset(BITCOMPS));  // open: Qn, preset
  not not_10 (NOTLONGSAVED_DISABLED, LONGSAVED);
  and and_15 (and_15_out, not_9_out, or_5_out);
  S_R_Flip_Flop s_r_ff_3 (
    .S(ARB_S0_SET), .R(ARB_S0_RESET), .clk(CLK), .Q(ARB_STATE_0_BIT), .reset(not_11_out));  // open: Qn, preset
  not not_11 (not_11_out, ENA);
  S_R_Flip_Flop s_r_ff_4 (
    .S(EVENBIT), .R(1'b0), .clk(NOT_LONG_SAVED), .Q(TX1), .reset(ONECYCLE_COMPLETED));  // open: Qn, preset
  D_Flip_Flop d_ff_3 (.D(TRANSMIT_DATA_BIT1), .clk(CLK), .Q(ONECYCLE_COMPLETED), .reset(TO_IDLE));  // open: Qn, preset
  D_Flip_Flop d_ff_4 (.D(LONGSAVED), .clk(CLK), .Q(d_ff_4_q), .reset(TO_IDLE));  // open: Qn, preset
  not not_12 (LONGSAVED_DISABLED, NOT_LONG_SAVED);
  or or_7 (NOTLONGSAVED_RESET, ONECYCLE_COMPLETED, not_13_out);
  D_Flip_Flop d_ff_5 (.D(d_ff_4_q), .clk(CLK), .Q(d_ff_5_q), .reset(TO_IDLE));  // open: Qn, preset
  or or_8 (LOSS_B1, ARBL_LOSS_BIT1_1, ARBL_LOSS_BIT1);
  or or_9 (or_9_out, BITCOMP_TO_BIT1, and_15_out);
  not not_13 (not_13_out, ENA);
  or or_10 (BIT1_2, ONECYCLE_COMPLETED, NOT_LONG_SAVED, TRANSMIT_DATA_BIT1);
  D_Flip_Flop d_ff_6 (.D(d_ff_5_q), .clk(CLK), .Q(BITCOMPS), .reset(TO_IDLE));  // open: Qn, preset
  or or_11 (BITCMP, BITCOMP_TO_BIT1, BITCOMP_TO_IDLE, BITCMP_c);
  or or_12 (TX, TX1, TX2);
  or or_13 (TO_IDLE, NOTLONGSAVED_RESET, LONGSAVED_RESET, TO_RESET);
  or or_14 (ARBL, ARBL_LOSS_BIT1, ARBL_LOSS_BIT2);
  or or_15 (LOSS_B2, ARBL_LOSS_BIT2, ARBL_LOSS_BIT2_1);
  not not_14 (not_14_out, IDLE_STATE);
  or or_16 (LONGSAVED_RESET, BITCOMPS, not_15_out);
  not not_15 (not_15_out, ENA);
  or or_17 (BIT2_2, BITCOMPS, d_ff_5_q, d_ff_4_q);
  and and_16 (BIT1_STATE, or_9_out, not_14_out);
  or or_18 (TRANSMITTING_DATA_IN_BIT2, d_ff_4_q, d_ff_5_q);
  or or_19 (or_19_out, BIT2, BIT2_2);
  or or_20 (ARB_S0_RESET, ARB_S0_RESET_FROM_BIT1, ARB_S0_RESET_FROM_BIT1_a, 1'b0);
  Multiplexer #(.select(2)) multiplexer_1 (
    .in0(1'b0), .in1(1'b0), .in2(1'b1), .out(LONG), .sel({LONG_STATE, NOT_LONG_STATE}));  // open: in3
  xnor xnor_1 (xnor_1_out, DOUT, EVENBIT);
  not not_16 (not_16_out, xnor_1_out);
  or or_21 (or_21_out, BIT1, or_19_out);
  and and_17 (NOT_LONG_STATE, xnor_1_out, BIT1);
  and and_18 (LONG_STATE, not_16_out, or_21_out);
  or or_22 (ARB_S1_RESET, ARB_S1_RESET_FROM_BIT2, ARB_S0_SET_FROM_BIT2, 1'b0);
  Demultiplexer #(.select(2)) demultiplexer_1 (
    .out0(BITCMP_c), .out1(BIT1), .out2(BIT2), .in(1'b1), .sel({ARB_STATE_1_BIT, and_19_out[0]}));  // open: out3
  and and_19 (and_19_out[0], ARB_STATE_0_BIT, not_17_out);
  not not_17 (not_17_out, TO_IDLE);

  // Other names for the same wires on the sheet: ARB_S1_SET_FROM_BIT1 = ARB_S0_RESET_FROM_BIT1_a;
  //   BITCMP_a = ARB_S1_RESET_FROM_BIT2; ARB_S1_RESET_FROM_BIT2_a = ARB_S0_SET_FROM_BIT2;
  //   BITCMP_b = ARB_S0_SET_FROM_BIT2; DW_1 = DW; IDLE = BITCMP_c; LONG_1 = LONG; TWOCYCLE_DONE = BITCOMPS

  // Notes on the sheet:
  //   BIT1 State logic
  //   BIT2 State logic
  //   For detecting zero comaprison
  //   For detecting zero comparison
  //   F
endmodule

module VPWBObserver (
  input  RX,
  input  ENA,
  input  CLK,
  output IDLE,
  output DIN,
  output NEWBIT
);

  wire and_1_out, and_3_out, and_4_out, and_5_out, and_6_out, and_7_out, and_8_out, and_11_out, and_12_out,
       and_16_out, and_18_out, B0, B00, B1, B11, BACK_TO_B1, BACK_TO_B1_1, BACK_TO_E1, BACK_TO_E1_2,
       BACK_TO_E1_3, d_ff_4_qn, DIN_0, DIN_1, E0, E00, E1, IDLE_B00, IDLE_E00, INITIAL_IDLE, NEWBIT2,
       NEWBIT3, NEWBIT4, NEWBITZ, not_2_out, not_3_out, not_4_out, not_5_out, not_6_out, not_7_out,
       not_8_out, not_9_out, not_10_out, not_11_out, not_12_out, not_13_out, not_14_out, not_15_out,
       NOT_IN_E_STATES, NOT_INITIAL_IDLE, NOT_INITIAL_IDLE_1, or_2_out, or_4_out, TO_B1, ZERO;

  not not_1 (ZERO, RX);
  and and_1 (and_1_out, B0, RX);
  and and_2 (NEWBITZ, B1, NOT_IN_E_STATES, ZERO);
  D_Flip_Flop d_ff_1 (.D(and_1_out), .clk(CLK), .Q(BACK_TO_B1));  // open: Qn, preset, reset
  and and_3 (and_3_out, B00, ZERO);
  and and_4 (and_4_out, E1, ZERO);
  D_Flip_Flop d_ff_2 (.D(and_4_out), .clk(CLK), .Q(E0));  // open: Qn, preset, reset
  and and_5 (and_5_out, E1, RX);
  not not_2 (not_2_out, ENA);
  D_Flip_Flop d_ff_3 (.D(and_3_out), .clk(CLK), .Q(IDLE_B00));  // open: Qn, preset, reset
  and and_6 (and_6_out, E0, RX);
  and and_7 (and_7_out, E00, RX);
  and and_8 (and_8_out, E00, ZERO);
  not not_3 (not_3_out, B11);
  and and_9 (NEWBIT4, B11, NEWBITZ);
  D_Flip_Flop d_ff_4 (.D(RX), .clk(CLK), .Q(B1), .Qn(d_ff_4_qn), .reset(not_2_out));  // open: preset
  D_Flip_Flop d_ff_5 (.D(NEWBITZ), .clk(CLK), .Q(B0), .reset(E0));  // open: Qn, preset
  D_Flip_Flop d_ff_6 (.D(and_5_out), .clk(CLK), .Q(BACK_TO_E1_3));  // open: Qn, preset, reset
  D_Flip_Flop d_ff_7 (.D(and_6_out), .clk(CLK), .Q(BACK_TO_E1));  // open: Qn, preset, reset
  D_Flip_Flop d_ff_8 (.D(and_7_out), .clk(CLK), .Q(BACK_TO_E1_2));  // open: Qn, preset, reset
  D_Flip_Flop d_ff_9 (.D(and_8_out), .clk(CLK), .Q(IDLE_E00));  // open: Qn, preset, reset
  or or_1 (NEWBIT2, BACK_TO_B1, BACK_TO_B1_1);
  and and_10 (NEWBIT3, NEWBITZ, not_3_out);
  D_Flip_Flop d_ff_10 (.D(E0), .clk(CLK), .Q(E00));  // open: Qn, preset, reset
  or or_2 (or_2_out, NEWBIT3, NEWBIT2, NEWBIT4);
  and and_11 (and_11_out, B1, RX);
  and and_12 (and_12_out, B0, ZERO);
  not not_4 (not_4_out, E1);
  not not_5 (not_5_out, E00);
  not not_6 (not_6_out, E0);
  D_Flip_Flop d_ff_11 (.D(and_11_out), .clk(CLK), .Q(B11), .reset(not_2_out));  // open: Qn, preset
  D_Flip_Flop d_ff_12 (.D(and_12_out), .clk(CLK), .Q(B00));  // open: Qn, preset, reset
  and and_13 (BACK_TO_B1_1, B00, RX);
  buf or_3 (NEWBIT, or_2_out);  // OR_Gate
  and and_14 (TO_B1, B11, not_4_out, not_5_out, not_6_out, ZERO);
  and and_15 (NOT_IN_E_STATES, not_5_out, not_4_out, not_6_out);
  D_Flip_Flop d_ff_13 (.D(and_16_out), .clk(CLK), .Q(E1), .reset(not_2_out));  // open: Qn, preset
  and and_16 (and_16_out, B11, RX);
  or or_4 (or_4_out, BACK_TO_B1, TO_B1);
  not not_7 (not_7_out, or_4_out);
  not not_8 (not_8_out, NOT_INITIAL_IDLE_1);
  and and_17 (DIN, not_7_out, NEWBIT);
  D_Flip_Flop #(.trigger("high")) d_ff_14 (.D(BACK_TO_B1), .clk(CLK), .Q(DIN_0));  // open: Qn, preset, reset
  D_Flip_Flop d_ff_15 (.D(TO_B1), .clk(CLK), .Q(DIN_1));  // open: Qn, preset, reset
  Multiplexer multiplexer_1 (.in0(1'b0), .in1(1'b1), .out(INITIAL_IDLE), .sel(and_18_out));
  and and_18 (and_18_out, not_8_out, NOT_INITIAL_IDLE);
  not not_9 (not_9_out, B11);
  not not_10 (not_10_out, B0);
  not not_11 (not_11_out, B00);
  not not_12 (not_12_out, E1);
  not not_13 (not_13_out, E0);
  not not_14 (not_14_out, E00);
  not not_15 (not_15_out, B1);
  and and_19 (NOT_INITIAL_IDLE, not_9_out, not_10_out, not_11_out, not_12_out, not_13_out, not_14_out, not_15_out);
  or or_5 (IDLE, IDLE_B00, IDLE_E00, INITIAL_IDLE);
  or or_6 (NOT_INITIAL_IDLE_1, B11, B0, B00, E1, E0, E00, B1);

  // Other names for the same wires on the sheet: IDLE_STATE = IDLE; ONE = RX
endmodule

module TEST (
  input  in_1
);

  wire clock_1_out, d_ff_1_qn, not_1_out;

  Clock clock_1 (.out(clock_1_out));
  D_Flip_Flop d_ff_1 (.D(in_1), .clk(clock_1_out), .Qn(d_ff_1_qn));  // open: Q, preset, reset
  D_Flip_Flop d_ff_2 (.D(in_1), .clk(not_1_out));  // open: Q, Qn, preset, reset
  not not_1 (not_1_out, d_ff_1_qn);
endmodule
